// Digital circuit hazard_unit.dig as structural Verilog
module hazard_unit (
  input  [4:0] RR0_2,
  input  [4:0] RR1_2,
  input  [4:0] WR_4,
  input  [4:0] WR_3,
  input  RFW_4,
  input  RFW_3,
  input  CLR,
  input  PCbr2,
  output [1:0] FRD_0_Sel,
  output [1:0] FRD_1_Sel,
  output FLUSH
);

  wire and_1_out, and_2_out, and_3_out, and_4_out, comparator_1_eq, comparator_2_eq, comparator_3_eq,
       comparator_4_eq;

  Comparator #(.Bits(5)) comparator_1 (.a(RR0_2), .b(WR_4), .eq(comparator_1_eq));  // open: gt, lt
  Comparator #(.Bits(5)) comparator_2 (.a(RR0_2), .b(WR_3), .eq(comparator_2_eq));  // open: gt, lt
  Comparator #(.Bits(5)) comparator_3 (.a(RR1_2), .b(WR_4), .eq(comparator_3_eq));  // open: gt, lt
  Comparator #(.Bits(5)) comparator_4 (.a(RR1_2), .b(WR_3), .eq(comparator_4_eq));  // open: gt, lt
  and and_1 (and_1_out, comparator_1_eq, RFW_4);
  and and_2 (and_2_out, comparator_2_eq, RFW_3);
  and and_3 (and_3_out, comparator_3_eq, RFW_4);
  and and_4 (and_4_out, comparator_4_eq, RFW_3);
  or or_1 (FLUSH, CLR, PCbr2);
  PriorityEncoder #(.Selector_Bits(2)) priorityencoder_1 (
    .in0(1'b1), .in1(and_1_out), .in2(and_2_out), .in3(1'b0), .num(FRD_0_Sel));  // open: any
  PriorityEncoder #(.Selector_Bits(2)) priorityencoder_2 (
    .in0(1'b1), .in1(and_3_out), .in2(and_4_out), .in3(1'b0), .num(FRD_1_Sel));  // open: any
endmodule
